# Fritzing sketch resonet (saved by Fritzing 1.0.4)
breadboards: 1

parts:
  A1 = Adafruit ADS1115 ADC
  A2 = Raspberry Pi 5
  J2 = Piezo Speaker
  J4 = Piezo Speaker
  D1 = Diode [package=diode-1n4001]
  D2 = Diode [package=diode-1n4001]
  D3 = Diode [package=diode-1n4001]
  D4 = Diode [package=diode-1n4001]
  D5 = Diode [package=diode-1n4001]
  D6 = Diode [package=diode-1n4001]
  D7 = Diode [package=diode-1n4001]
  D8 = Diode [package=diode-1n4001]
  J5 = Piezo Speaker
  J6 = Piezo Speaker

nets:
  GND: A1.GND, A2.GND, J6.pin1
  N1: A1.A0, D4.C, D8.A
  N2: A1.A1, J2.pin2
  N3: A1.A2, D2.C, D6.A, J5.pin2
  N4: A1.A3, D1.C
  N5: J4.pin1, D5.C
  N6: D2.A, D8.C
  N7: D3.C, D7.A

custom parts:
  Raspberry Pi 5: The RPi5, a faster version of the awesome Raspberry Pi4B ARM Board with 40 pin gpio.
